// Logisim project cpu.circ as structural Verilog: 1 circuit, main circuit main
module main (
  input  [15:0] in_1,
  input  [7:0] in_2,
  input  in_3,
  input  in_4,
  input  IP_HI_TO_DATA,
  input  IP_LO_TO_DATA,
  input  DATA_TO_IP_HI,
  input  DATA_TO_IP_LO,
  input  IP_TO_ADDR,
  input  IP_INC,
  input  ADDR_TO_IP,
  output [7:0] out_12,
  output [15:0] out_13,
  output [15:0] Instruction_Pointer
);

  wire CLK, nor_1_out, nor_2_out, or_1_out, RST;
  wire [7:0] controlled_buffer_3_out, controlled_buffer_6_out;

  Button u_CLK (.out(CLK));
  Button u_RST (.out(RST));
  assign out_12 = in_3 ? in_2 : 8'bz;  // Controlled_Buffer controlled_buffer_1
  assign out_12 = IP_LO_TO_DATA ? Instruction_Pointer[7:0] : 8'bz;  // Controlled_Buffer controlled_buffer_2
  assign controlled_buffer_3_out = DATA_TO_IP_LO ? out_12 : 8'bz;  // Controlled_Buffer controlled_buffer_3
  assign out_12 = IP_HI_TO_DATA ? Instruction_Pointer[15:8] : 8'bz;  // Controlled_Buffer controlled_buffer_4
  nor nor_1 (nor_1_out, DATA_TO_IP_LO, ADDR_TO_IP);
  assign controlled_buffer_3_out = nor_1_out ? Instruction_Pointer[7:0] : 8'bz;  // Controlled_Buffer controlled_buffer_5
  assign controlled_buffer_6_out = DATA_TO_IP_HI ? out_12 : 8'bz;  // Controlled_Buffer controlled_buffer_6
  nor nor_2 (nor_2_out, DATA_TO_IP_HI, ADDR_TO_IP);
  assign controlled_buffer_6_out = nor_2_out ? Instruction_Pointer[15:8] : 8'bz;  // Controlled_Buffer controlled_buffer_7
  or or_1 (or_1_out, DATA_TO_IP_HI, DATA_TO_IP_LO, ADDR_TO_IP);
  Counter #(.width(16), .max('hffff)) IP (
    .load(or_1_out), .D({controlled_buffer_6_out, controlled_buffer_3_out}), .count(IP_INC),
    .Q(Instruction_Pointer), .clk(CLK), .clr(RST));  // open: carry
  assign {controlled_buffer_6_out, controlled_buffer_3_out} = ADDR_TO_IP ? out_13 : 16'bz;  // Controlled_Buffer controlled_buffer_8
  assign out_13 = in_4 ? in_1 : 16'bz;  // Controlled_Buffer controlled_buffer_9
  assign out_13 = IP_TO_ADDR ? Instruction_Pointer : 16'bz;  // Controlled_Buffer controlled_buffer_10
endmodule
